// Logisim project CtrlUnit.circ as structural Verilog: 1 circuit, main circuit main
module main (
  input  [3:0] OpCode,
  output bra,
  output branch,
  output regWrite,
  output RegDes,
  output AluSrc,
  output MemR,
  output MenW
);

  wire boz_out, comp_out, stri_out;

  and load (MemR, ~OpCode[3], ~OpCode[2], ~OpCode[1], ~OpCode[0]);  // AND_Gate
  and store (MenW, ~OpCode[3], ~OpCode[2], OpCode[1], ~OpCode[0]);  // AND_Gate
  and stri (stri_out, ~OpCode[3], OpCode[2], ~OpCode[1], ~OpCode[0]);  // AND_Gate
  and boz (boz_out, ~OpCode[3], OpCode[2], OpCode[1], ~OpCode[0]);  // AND_Gate
  and u_bra (bra, OpCode[3], ~OpCode[2], ~OpCode[1], ~OpCode[0]);  // AND_Gate
  and comp (comp_out, OpCode[3], ~OpCode[2], OpCode[1], ~OpCode[0]);  // AND_Gate
  or or_1 (branch, boz_out, bra);
  or or_2 (regWrite, OpCode[0], comp_out, stri_out, MemR);
  and and_1 (RegDes, ~stri_out, ~MenW, ~MemR);  // AND_Gate
  or or_3 (AluSrc, stri_out, MenW, MemR);
endmodule
