// Logisim project CPU.circ as structural Verilog: 1 circuit, main circuit main
module main (
  input  in_1
);

  wire boz, Branch, clock_1_out, comparator_1_eq, main_1_alusrc, main_1_boz, main_1_branch, main_1_memr,
       main_1_memtoreg, main_1_memw, main_1_regdes, main_1_regwrite, nand_1_out;
  wire [3:0] multiplexer_1_out;
  wire [15:0] adder_1_out, and_1_out, bit_extender_1_out, bit_extender_2_out, main_2_rs_data, main_2_rt_data,
       main_3_alu_out, multiplexer_2_out, multiplexer_3_out, multiplexer_4_out, multiplexer_5_out,
       multiplier_1_out, or_1_out, Pc_q, ram_1_data, rom_1_data;

  Clock clock_1 (.out(clock_1_out));
  Register #(.width(16)) Pc (.D(multiplexer_4_out), .Q(Pc_q), .clk(clock_1_out), .clr(in_1));  // open: en
  CtrlUnit_main main_1 (
    .OpCode(rom_1_data[3:0]), .branch(main_1_branch), .regWrite(main_1_regwrite), .RegDes(main_1_regdes),
    .AluSrc(main_1_alusrc), .MemR(main_1_memr), .MemW(main_1_memw), .MemToReg(main_1_memtoreg),
    .boz(main_1_boz));
  Adder #(.width(16)) adder_1 (.a(16'h2), .b(Pc_q), .out(adder_1_out));  // open: cin, cout
  ROM #(.addrWidth(16), .dataWidth(16)) rom_1 (.addr(Pc_q), .data(rom_1_data));  // open: sel
  Comparator #(.width(4)) comparator_1 (.a(4'b0000), .b(rom_1_data[3:0]), .eq(comparator_1_eq));  // open: gt, lt
  assign bit_extender_1_out = {{4{1'b0}}, rom_1_data[15:4]};  // Bit_Extender bit_extender_1
  Multiplexer #(.width(4), .disabled(0), .enable("false")) multiplexer_1 (
    .in0(rom_1_data[11:8]), .in1(rom_1_data[15:12]), .out(multiplexer_1_out), .sel(main_1_regdes));
  assign bit_extender_2_out = {{12{rom_1_data[15]}}, rom_1_data[15:12]};  // Bit_Extender bit_extender_2
  Multiplier #(.width(16)) multiplier_1 (.a(bit_extender_1_out), .b(16'h2), .out(multiplier_1_out));  // open: cin, cout
  nand nand_1 (nand_1_out, comparator_1_eq, boz);
  Multiplexer #(.width(16), .disabled(0), .enable("false")) multiplexer_2 (
    .in0(multiplier_1_out), .in1(rom_1_data), .out(multiplexer_2_out), .sel(nand_1_out));
  Register_File_2_0_main main_2 (
    .RegWrite(main_1_regwrite), .Rd(multiplexer_1_out), .WriteData(multiplexer_5_out), .Rs(rom_1_data[7:4]),
    .Rt(rom_1_data[11:8]), .Clock(clock_1_out), .Rs_Data(main_2_rs_data), .Rt_Data(main_2_rt_data));
  Multiplexer #(.width(16), .disabled(0), .enable("false")) multiplexer_3 (
    .in0(main_2_rt_data), .in1(bit_extender_2_out), .out(multiplexer_3_out), .sel(main_1_alusrc));
  assign and_1_out = 16'hfe00 & Pc_q;  // AND_Gate and_1, 16 bits wide
  ALU_main main_3 (.In1(main_2_rs_data), .In2(multiplexer_3_out), .OpCode(rom_1_data[3:0]), .ALU_out(main_3_alu_out));
  assign or_1_out = multiplexer_2_out | and_1_out;  // OR_Gate or_1, 16 bits wide
  Multiplexer #(.width(16), .disabled(0), .enable("false")) multiplexer_4 (
    .in0(adder_1_out), .in1(or_1_out), .out(multiplexer_4_out), .sel(Branch));
  RAM #(.addrWidth(16), .dataWidth(16), .bus("separate")) ram_1 (
    .addr(main_3_alu_out), .din(main_2_rt_data), .data(ram_1_data), .str(main_1_memw), .clk(clock_1_out),
    .ld(main_1_memr));  // open: sel, clr
  Multiplexer #(.width(16), .disabled(0), .enable("false")) multiplexer_5 (
    .in0(main_3_alu_out), .in1(ram_1_data), .out(multiplexer_5_out), .sel(main_1_memtoreg));
endmodule
